# Fritzing sketch Circuit Sketch (saved by Fritzing 0.9.0b)
circuit board: 1.57523cm x 0.895466cm
breadboards: 1

parts:
  J1 = female pin header, 3 pins [form="♀ (female)"]
  R1 = Resistor [tolerance=±5% resistance=220 package="1206 [SMD]"]
  J2 = screw terminal, 3 pins

nets:
  N1: J1.pin1, R1.Pin_1, J2.pin3
  N2: J1.pin2, J2.pin2
  N3: J1.pin3, R1.Pin_0, J2.pin1
